// Logisim project control_logic.circ as structural Verilog: 1 circuit, main circuit control_logic
module control_logic (
  input  [31:0] inst,
  input  BrEq,
  input  BrLt,
  output PCSel,
  output RegWEn,
  output [2:0] ImmSel,
  output BrUn,
  output ASel,
  output BSel,
  output [3:0] ALUSel,
  output MemRW,
  output [1:0] WBSel,
  output CSRSel,
  output CSRWen
);

  wire comparator_1_eq, comparator_2_eq, comparator_4_eq, comparator_5_eq, or_1_out;
  wire [3:0] rom_1_data;

  ROM #(.addrWidth(5), .dataWidth(4)) rom_1 (.addr({inst[14:12], inst[30], inst[25]}), .data(rom_1_data));
  Comparator #(.width(7)) comparator_1 (.a(inst[6:0]), .b(7'b0110011), .eq(comparator_1_eq));  // open: gt, lt
  Comparator #(.width(7)) comparator_2 (.a(inst[6:0]), .b(7'b0010011), .eq(comparator_2_eq));  // open: gt, lt
  Comparator #(.width(7)) comparator_3 (.a(inst[6:0]), .b(7'b0010011), .eq(BSel));  // open: gt, lt
  Multiplexer #(.enable("false"), .width(4)) multiplexer_1 (
    .in0(4'b0000), .in1(rom_1_data), .out(ALUSel), .sel(or_1_out));
  or or_1 (or_1_out, comparator_1_eq, comparator_2_eq);
  Comparator #(.width(7)) comparator_4 (.a(inst[6:0]), .b(7'b0110011), .eq(comparator_4_eq));  // open: gt, lt
  Comparator #(.width(7)) comparator_5 (.a(inst[6:0]), .b(7'b0010011), .eq(comparator_5_eq));  // open: gt, lt
  or or_2 (RegWEn, comparator_4_eq, comparator_5_eq);

  assign ASel = 1'b0;
  assign MemRW = 1'b0;
  assign PCSel = 1'b0;
  assign WBSel = 2'b01;

  // Other names for the same wires on the sheet: opcode[6:0] = inst[6:0]; rd[4:0] = inst[11:7];
  //   func3[2:0] = inst[14:12]; rs1[4:0] = inst[19:15]; rs2[4:0] = inst[24:20]; func7[6:0] = inst[31:25]

  // Notes on the sheet:
  //   INPUTS to your circuit
  //   Docode
  //   contents of rom_1 (hex, n*v repeats v):
  //   0 a c 0 6 e 0 0 7 4*0 b 0 0 3 0 0 0 4 0 5 0 2 0 0 0 1
  //   R-instr
  //   I-instr
  //   DON'T CHANGE THE LOCATIONS OF THE INPUTS AND OUTPUTS!
  //   OUTPUT from your circuit
endmodule
