// Logisim project cpu.circ as structural Verilog: 1 circuit, main circuit cpu
module cpu (
  input  clk,
  input  [31:0] INSTRUCTION,
  input  [31:0] READ_DATA,
  output [31:0] WRITE_ADDRESS,
  output [31:0] PROGRAM_COUNTER,
  output [31:0] ra,
  output [31:0] sp,
  output [31:0] t0,
  output [31:0] t1,
  output [31:0] t2,
  output [31:0] s0,
  output [31:0] s1,
  output [31:0] a0,
  output [31:0] tohost,
  output [3:0] WRITE_ENABLE,
  output [31:0] WRITE_DATA
);

  wire RegWEn;
  wire [1:0] WBsel;
  wire [2:0] func3, ImmSel;
  wire [3:0] ALUSel;
  wire [11:0] imm;
  wire [19:0] INSTRUCTION2;
  wire [31:0] adder_1_out, ALU_output, complete_Imm, r1, r2, WB_data;

  Adder #(.width(32)) adder_1 (.a(PROGRAM_COUNTER), .b(32'h4), .out(adder_1_out));  // open: cin, cout
  Register #(.width(32)) PC (.D(adder_1_out), .clk(clk), .Q(PROGRAM_COUNTER));  // open: en, clr
  Register #(.width(32)) register_1 (
    .D(INSTRUCTION), .clk(clk), .Q({imm, INSTRUCTION2[19:15], func3, INSTRUCTION2[11:0]}));  // open: en, clr
  control_logic control_logic_1 (
    .RegWEn(RegWEn), .ImmSel(ImmSel), .ALUSel(ALUSel), .WBSel(WBsel), .inst(INSTRUCTION));  // open: CSRWen, PCSel, BrUn, ASel, BSel, MemRW, CSRSel, BrEq, BrLt
  regfile regfile_1 (
    .rs1(INSTRUCTION2[19:15]), .rd(INSTRUCTION2[11:7]), .Write_Data(WB_data), .RegWEn(RegWEn), .clk(clk),
    .ra(ra), .sp(sp), .t0(t0), .t1(t1), .t2(t2), .s0(s0), .s1(s1), .a0(a0), .Read_Data_1(r1), .Read_Data_2(r2));  // open: rs2
  imm_gen imm_gen_1 (.inst({imm, INSTRUCTION2[19:15], func3, INSTRUCTION2[11:0]}), .ImmSel(ImmSel), .imm(complete_Imm));
  alu alu_1 (.Result(ALU_output), .A(r1), .B(complete_Imm), .ALUSel(ALUSel));
  csr csr_1 (.tohost(tohost));  // open: CSR_address, CSR_din, CSR_WE, clk
  // branch_comp branch_comp_1: pin names not known
  Multiplexer #(.enable("false"), .select(2), .width(32)) multiplexer_1 (
    .in1(ALU_output), .in2(READ_DATA), .out(WB_data), .sel(WBsel));  // open: in0, in3

  // Other names for the same wires on the sheet: opcode[6:0] = INSTRUCTION2[6:0]; rd[4:0] = INSTRUCTION2[11:7];
  //   INSTRUCTION2 (some bits) = {imm, func3}; rs1[4:0] = INSTRUCTION2[19:15]

  // Notes on the sheet:
  //   Output to IMEM
  //   IMEM (do **NOT** move this)
  //   Inputs from IMEM
  //   It is OK to move the PC, RegFile, ALU, MEM, Branch Comp, Imm Gen, and Control Logic to wherever is most convenient for you when constructing your CPU, and to delete this text
  //   Inputs/Outputs for testing. Do **NOT** move these.
  //   Outputs To DMEM
  //   DMEM (do **NOT** move this)
  //   Inputs From DMEM
endmodule
